# Fritzing sketch Bewegungssensor (saved by Fritzing 0.9.3b)
breadboards: 1

parts:
  Bauteil1 = Arduino Uno (Rev3)
  R1 = Resistor [tolerance=±10% resistance=220 package=THT]
  LED1 = LED - 5mm [color="Red (633nm)" package="5 mm [THT]"]
  U1 = TOUCH [package=touch2]  # not connected

nets:
  N1: Bauteil1.A2, R1.Pin_0, LED1.cathode
