# Fritzing sketch Lichter (saved by Fritzing 0.9.3b)
breadboards: 1

parts:
  Bauteil1 = Arduino Uno (Rev3)
  S1 = Pushbutton [package="[SMD]"]
  R1 = Resistor [tolerance=±5% resistance=220 package=THT]
  R2 = Resistor [tolerance=±5% resistance=220 package=THT]
  R3 = Resistor [tolerance=±5% resistance=220 package=THT]
  R4 = Resistor [tolerance=±5% resistance=220 package=THT]
  R5 = Resistor [tolerance=±5% resistance=220 package=THT]
  R6 = Resistor [tolerance=±5% resistance=220 package=THT]
  LED1 = LED - 5mm [color="Red (633nm)" package="5 mm [THT]"]
  LED2 = LED - 5mm [color="Red (633nm)" package="5 mm [THT]"]
  LED3 = LED - 5mm [color="Red (633nm)" package="5 mm [THT]"]
  LED4 = LED - 5mm [color="Red (633nm)" package="5 mm [THT]"]
  LED5 = LED - 5mm [color="Red (633nm)" package="5 mm [THT]"]

nets:
  N1: Bauteil1.A2, S1.Pin_1, S1.Pin_2, R1.Pin_0, LED1.anode, LED2.anode, LED4.anode, LED5.anode
  N2: Bauteil1.D9_PWM, R2.Pin_0
  N3: Bauteil1.GND, S1.Pin_3, S1.Pin_4, R1.Pin_1
  N4: R2.Pin_1, LED5.cathode
  N5: R3.Pin_1, LED1.cathode
  N6: R4.Pin_1, LED2.cathode
  N7: R5.Pin_1, LED3.cathode
  N8: R6.Pin_1, LED4.cathode
